# Fritzing sketch lazy-trinket (saved by Fritzing 0.9.3b)
breadboards: 1

parts:
  Part2 = Adafruit Trinket M0 [part_number="Adafruit #3500"]
  Part3 = Adafruit VL6180X Time of Flight Distance Sensor [part_number="Adafruit #3316"]
  J1 = Piezo Speaker

nets:
  GND: Part2.GND, Part3.GND, J1.pin1
  3.3V: Part2.3.3V, Part3.VIN
  N1: Part2.D2_A1_PA09_SCL_MISO, Part3.SCL
  N2: Part2.D1_A0_PA02, J1.pin2
  N3: Part2.D0_A4_PA08_SDA, Part3.SDA

custom parts:
  Adafruit VL6180X Time of Flight Distance Sensor: The VL6180X is a Time of Flight distance sensor like no other you've used! The sensor contains a very tiny invisible laser source, and a matching sensor. The VL6180X can detect the "time of flight", or how long the light has taken to bounce back to the sensor. Since it uses a very narrow light source, it is good for determining distance of only the surface directly in front of it. Unlike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
